// Logisim project PROCESSADOR_TESTE.circ as structural Verilog: 3 circuits, main circuit REGFIEL
// PROCESSOR
module main (
  input  in_1,
  input  in_2,
  input  in_3
);

  wire CLK, DATA, LOAD, MOV;
  wire [2:0] OP, RD;
  wire [2:1] RA;
  wire [3:0] alu_1_o, controlled_buffer_1_out, NUM, regfiel_1_a, regfiel_1_b;
  wire [7:0] counter_1_q;
  wire [15:0] rom_1_data;
  wire [15:9] register_1_q;

  Clock clock_1 (.out(CLK));
  Counter counter_1 (.load(1'b0), .count(1'b1), .Q(counter_1_q), .clk(CLK), .clr(1'b0));  // open: D, carry
  Hex_Digit_Display hex_digit_display_1 (.value(counter_1_q[7:4]));  // open: dp
  assign controlled_buffer_1_out = MOV ? NUM : 4'bz;  // Controlled_Buffer controlled_buffer_1
  Hex_Digit_Display hex_digit_display_2 (.value(counter_1_q[3:0]));  // open: dp
  ROM #(.dataWidth(16)) rom_1 (.addr(counter_1_q), .data(rom_1_data));  // open: sel
  RAM #(.addrWidth(3), .dataWidth(3), .bus("separate")) ram_1 (
    .addr({RA, NUM[3]}), .data(NUM[2:0]), .clk(in_2), .ld(in_3), .clr(in_1));  // open: din, str, sel
  REGFIEL regfiel_1 (
    .INP(controlled_buffer_1_out), .C(CLK), .A(regfiel_1_a), .RA({RA, NUM[3]}), .RD(RD), .B(regfiel_1_b),
    .RB(NUM[2:0]));
  assign controlled_buffer_1_out = DATA ? alu_1_o : 4'bz;  // Controlled_Buffer controlled_buffer_2
  Register #(.width(16)) register_1 (
    .D(rom_1_data), .en(1'b1), .Q({register_1_q[15:14], OP, register_1_q[10:9], RA, NUM, RD}), .clk(CLK));  // open: clr
  // XOR_Gate xor_1: pin names not known; wires that end beside it: LOAD, register_1_q[14], register_1_q[15]
  and and_1 (MOV, register_1_q[14], register_1_q[15]);
  ALU alu_1 (.A(regfiel_1_a), .B(regfiel_1_b), .O(alu_1_o), .OP(OP));
  buf and_2 (DATA, ~register_1_q[14]);  // AND_Gate AND_Gate

  // Other names for the same wires on the sheet: RB[2:0] = NUM[2:0]; RA[0] = NUM[3]

  // Notes on the sheet:
  //   c010, c019, 000a, 3844, c00d, 282e, 3184
  //   contents of rom_1 (hex, n*v repeats v):
  //   c010 c019 a 3844 c00d 282e 3184
  //   10xx xxxx xx00 0100
  //   8004
  //   LOAD RB(Ram0), RD(R4)
  //   LOAD LER DA RAM E JOGAR NO REG
endmodule

// REGFILE
module REGFIEL (
  input  [3:0] INP,
  input  C,
  input  [2:0] RA,
  input  [2:0] RD,
  input  [2:0] RB,
  output [3:0] A,
  output [3:0] B
);

  wire demultiplexer_1_out0, demultiplexer_1_out1, demultiplexer_1_out2, demultiplexer_1_out3,
       demultiplexer_1_out4, demultiplexer_1_out5, demultiplexer_1_out6, demultiplexer_1_out7;
  wire [3:0] R1_q, R2_q, R3_q, R4_q, R5_q, R6_q, R7_q, RO_q;

  Demultiplexer #(.select(3), .enable("true")) demultiplexer_1 (
    .out0(demultiplexer_1_out0), .out1(demultiplexer_1_out1), .out2(demultiplexer_1_out2),
    .out3(demultiplexer_1_out3), .out4(demultiplexer_1_out4), .out5(demultiplexer_1_out5),
    .out6(demultiplexer_1_out6), .out7(demultiplexer_1_out7), .in(1'b1), .sel(RD));  // open: en
  Register #(.width(4)) RO (.D(INP), .en(demultiplexer_1_out0), .Q(RO_q), .clk(C));  // open: clr
  Register #(.width(4)) R1 (.D(INP), .en(demultiplexer_1_out1), .Q(R1_q), .clk(C));  // open: clr
  Register #(.width(4)) R2 (.D(INP), .en(demultiplexer_1_out2), .Q(R2_q), .clk(C));  // open: clr
  Register #(.width(4)) R3 (.D(INP), .en(demultiplexer_1_out3), .Q(R3_q), .clk(C));  // open: clr
  Register #(.width(4)) R4 (.D(INP), .en(demultiplexer_1_out4), .Q(R4_q), .clk(C));  // open: clr
  Register #(.width(4)) R5 (.D(INP), .en(demultiplexer_1_out5), .Q(R5_q), .clk(C));  // open: clr
  Register #(.width(4)) R6 (.D(INP), .en(demultiplexer_1_out6), .Q(R6_q), .clk(C));  // open: clr
  Register #(.width(4)) R7 (.D(INP), .en(demultiplexer_1_out7), .Q(R7_q), .clk(C));  // open: clr
  Multiplexer #(.select(3), .width(4), .enable("true")) multiplexer_1 (
    .in0(RO_q), .in1(R1_q), .in2(R2_q), .in3(R3_q), .in4(R4_q), .in5(R5_q), .in6(R6_q), .in7(R7_q), .out(A),
    .sel(RA));  // open: en
  Multiplexer #(.select(3), .width(4), .enable("true")) multiplexer_2 (
    .in0(RO_q), .in1(R1_q), .in2(R2_q), .in3(R3_q), .in4(R4_q), .in5(R5_q), .in6(R6_q), .in7(R7_q), .out(B),
    .sel(RB));  // open: en
endmodule

module ALU (
  input  [3:0] A,
  input  [3:0] B,
  input  [2:0] OP,
  output [3:0] O
);

  wire [3:0] adder_1_out, and_1_out, multiplier_1_out, or_1_out, shifter_1_out, shifter_2_out,
       subtractor_1_out, xor_1_out;

  Adder #(.width(4)) adder_1 (.a(A), .b(B), .out(adder_1_out), .cin(1'b0));  // open: cout
  Subtractor #(.width(4)) subtractor_1 (.a(A), .b(B), .out(subtractor_1_out), .bin(1'b0));  // open: bout
  assign and_1_out = A & B;  // AND_Gate and_1, 4 bits wide
  assign or_1_out = A | B;  // OR_Gate or_1, 4 bits wide
  assign xor_1_out = A ^ B;  // XOR_Gate xor_1, 4 bits wide
  Shifter #(.width(4)) shifter_1 (.in(A), .\dist (B[1:0]), .out(shifter_1_out));
  Shifter #(.width(4), .shift("lr")) shifter_2 (.in(A), .\dist (B[1:0]), .out(shifter_2_out));
  Multiplier #(.width(4)) multiplier_1 (.a(A), .b(B), .out(multiplier_1_out));  // open: cin, cout
  Multiplexer #(.select(3), .width(4), .enable("true")) multiplexer_1 (
    .in0(adder_1_out), .in1(subtractor_1_out), .in2(and_1_out), .in3(or_1_out), .in4(xor_1_out),
    .in5(shifter_1_out), .in6(shifter_2_out), .in7(multiplier_1_out), .out(O), .sel(OP));  // open: en
endmodule
